// Logisim project decoder24.circ as structural Verilog: 1 circuit, main circuit decoder24
module decoder24 (
  input  A0,
  input  A1,
  output Y0,
  output Y1,
  output Y2,
  output Y3
);

  wire n0, n1;

  not not_1 (n0, A0);
  not not_2 (n1, A1);
  and and_1 (Y0, n0, n1);
  and and_2 (Y1, A0, n1);
  and and_3 (Y2, n0, A1);
  and and_4 (Y3, A0, A1);
endmodule
