// Logisim project encoder164.circ as structural Verilog: 1 circuit, main circuit encoder164
module encoder164 (
  input  D0,
  input  D1,
  input  D2,
  input  D3,
  input  D4,
  input  D5,
  input  D6,
  input  D7,
  input  D8,
  input  D9,
  input  D10,
  input  D11,
  input  D12,
  input  D13,
  input  D14,
  input  D15,
  output Y0,
  output Y1,
  output Y2,
  output Y3
);

  wire n0, n1, n2, n3, n4, n5, n7, n8, n9, n10, n11, n12, n14, n15, n16, n17, n18, n19, n21, n22, n23, n24,
       n25, n26;

  or or_1 (n0, D1, D3);
  or or_2 (n1, n0, D5);
  or or_3 (n2, n1, D7);
  or or_4 (n3, n2, D9);
  or or_5 (n4, n3, D11);
  or or_6 (n5, n4, D13);
  or or_7 (Y0, n5, D15);
  or or_8 (n7, D2, D3);
  or or_9 (n8, n7, D6);
  or or_10 (n9, n8, D7);
  or or_11 (n10, n9, D10);
  or or_12 (n11, n10, D11);
  or or_13 (n12, n11, D14);
  or or_14 (Y1, n12, D15);
  or or_15 (n14, D4, D5);
  or or_16 (n15, n14, D6);
  or or_17 (n16, n15, D7);
  or or_18 (n17, n16, D12);
  or or_19 (n18, n17, D13);
  or or_20 (n19, n18, D14);
  or or_21 (Y2, n19, D15);
  or or_22 (n21, D8, D9);
  or or_23 (n22, n21, D10);
  or or_24 (n23, n22, D11);
  or or_25 (n24, n23, D12);
  or or_26 (n25, n24, D13);
  or or_27 (n26, n25, D14);
  or or_28 (Y3, n26, D15);
endmodule
