// Logisim project full_adder.circ as structural Verilog: 1 circuit, main circuit full_adder
module full_adder (
  input  A,
  input  B,
  input  Cin,
  output Sum,
  output Cout
);

  wire n0, n2, n3;

  // XOR_Gate xor_1: pin names not known; wires that end beside it: A, B, n0
  // XOR_Gate xor_2: pin names not known; wires that end beside it: n0, Cin, Sum
  and and_1 (n2, A, B);
  and and_2 (n3, n0, Cin);
  or or_1 (Cout, n2, n3);
endmodule
