// Logisim project minirv2_edges.circ as structural Verilog: 1 circuit, main circuit minirv2_edges
module minirv2_edges (
  input  Reset,
  output [31:0] PC_out,
  output [31:0] a0,
  output [31:0] ra,
  output illegal,
  output [31:0] x0_out,
  output [31:0] x2_out,
  output [31:0] x3_out,
  output [31:0] x4_out,
  output [31:0] x5_out,
  output [31:0] x6_out,
  output halt
);

  wire clock, n34, n36, n38, n39, n40, n41, n42, n43, n56, n57, n58, n59, n64, n65, n68, n69, n72, n73, n76,
       n77, n80, n81, n84, n85, n88, n89, n92, n93, n96, n97, n100, n101, n104, n105, n108, n109, n112, n113,
       n116, n117, n120, n121;
  wire [31:0] n23, n44, n45, n46, n49, n52, n60, n61, x7, x8, x9, x11, x12, x13, x14, x15;

  Clock clock_1 (.out(clock));
  and and_1 (n43, n40, n42);
  Comparator #(.width(2), .mode("unsigned")) comparator_1 (.a(n52[1:0]), .b(2'b00), .eq(n56));  // open: gt, lt
  Register #(.width(32)) PC (.D(n61), .en(n59), .Q(PC_out), .clk(clock), .clr(Reset));
  Comparator #(.width(4), .mode("unsigned")) comparator_2 (.a(n23[10:7]), .b(4'b0010), .eq(n68));  // open: gt, lt
  Register #(.width(32)) x3 (.D(n60), .en(n73), .Q(x3_out), .clk(clock), .clr(Reset));
  Comparator #(.width(4), .mode("unsigned")) comparator_3 (.a(n23[10:7]), .b(4'b0101), .eq(n80));  // open: gt, lt
  Register #(.width(32)) x6 (.D(n60), .en(n85), .Q(x6_out), .clk(clock), .clr(Reset));
  Comparator #(.width(4), .mode("unsigned")) comparator_4 (.a(n23[10:7]), .b(4'b1000), .eq(n92));  // open: gt, lt
  Register #(.width(32)) u_x9 (.D(n60), .en(n97), .Q(x9), .clk(clock), .clr(Reset));
  Comparator #(.width(4), .mode("unsigned")) comparator_5 (.a(n23[10:7]), .b(4'b1011), .eq(n104));  // open: gt, lt
  Register #(.width(32)) u_x12 (.D(n60), .en(n109), .Q(x12), .clk(clock), .clr(Reset));
  Comparator #(.width(4), .mode("unsigned")) comparator_6 (.a(n23[10:7]), .b(4'b1110), .eq(n116));  // open: gt, lt
  Register #(.width(32)) u_x15 (.D(n60), .en(n121), .Q(x15), .clk(clock), .clr(Reset));
  Comparator #(.width(7), .mode("unsigned")) comparator_7 (.a(n23[6:0]), .b(7'b1100111), .eq(n38));  // open: gt, lt
  Multiplexer #(.width(32), .select(4), .enable("false")) multiplexer_1 (
    .in0({32{1'b0}}), .in1(ra), .in2(x2_out), .in3(x3_out), .in4(x4_out), .in5(x5_out), .in6(x6_out),
    .in7(x7), .in8(x8), .in9(x9), .in10(a0), .in11(x11), .in12(x12), .in13(x13), .in14(x14), .in15(x15),
    .out(n44), .sel(n23[18:15]));
  Adder #(.width(32)) adder_1 (.a(PC_out), .b(32'h4), .out(n49), .cin(1'b0));  // open: cout
  not not_1 (n57, n38);
  and and_2 (n69, n59, n68);
  and and_3 (n81, n59, n80);
  and and_4 (n93, n59, n92);
  and and_5 (n105, n59, n104);
  and and_6 (n117, n59, n116);
  Comparator #(.width(32), .mode("unsigned")) comparator_8 (.a(PC_out), .b(32'h1c), .eq(halt));  // open: gt, lt
  or or_1 (n39, n36, n38);
  assign n45 = {{20{n23[31]}}, n23[31:20]};  // Bit_Extender bit_extender_1
  or or_2 (n58, n57, n56);
  Comparator #(.width(4), .mode("unsigned")) comparator_9 (.a(n23[10:7]), .b(4'b0001), .eq(n64));  // open: gt, lt
  Register #(.width(32)) x2 (.D(n60), .en(n69), .Q(x2_out), .clk(clock), .clr(Reset));
  Comparator #(.width(4), .mode("unsigned")) comparator_10 (.a(n23[10:7]), .b(4'b0100), .eq(n76));  // open: gt, lt
  Register #(.width(32)) x5 (.D(n60), .en(n81), .Q(x5_out), .clk(clock), .clr(Reset));
  Comparator #(.width(4), .mode("unsigned")) comparator_11 (.a(n23[10:7]), .b(4'b0111), .eq(n88));  // open: gt, lt
  Register #(.width(32)) u_x8 (.D(n60), .en(n93), .Q(x8), .clk(clock), .clr(Reset));
  Comparator #(.width(4), .mode("unsigned")) comparator_12 (.a(n23[10:7]), .b(4'b1010), .eq(n100));  // open: gt, lt
  Register #(.width(32)) u_x11 (.D(n60), .en(n105), .Q(x11), .clk(clock), .clr(Reset));
  Comparator #(.width(4), .mode("unsigned")) comparator_13 (.a(n23[10:7]), .b(4'b1101), .eq(n112));  // open: gt, lt
  Register #(.width(32)) u_x14 (.D(n60), .en(n117), .Q(x14), .clk(clock), .clr(Reset));
  Comparator #(.width(3), .mode("unsigned")) comparator_14 (.a(n23[14:12]), .b(3'b000), .eq(n34));  // open: gt, lt
  and and_7 (n40, n39, n34);
  assign n52 = n46 & 32'hfffffffe;  // AND_Gate and_8, 32 bits wide
  and and_9 (n59, n43, n58);
  and and_10 (n65, n59, n64);
  and and_11 (n77, n59, n76);
  and and_12 (n89, n59, n88);
  and and_13 (n101, n59, n100);
  and and_14 (n113, n59, n112);
  ROM #(.addrWidth(6), .dataWidth(32)) rom_1 (.addr(PC_out[7:2]), .data(n23));
  or or_3 (n41, n23[11], n23[19]);
  Adder #(.width(32)) adder_2 (.a(n44), .b(n45), .out(n46), .cin(1'b0));  // open: cout
  Multiplexer #(.width(32), .select(1), .enable("false")) multiplexer_2 (.in0(n46), .in1(n49), .out(n60), .sel(n38));
  Register #(.width(32)) x1 (.D(n60), .en(n65), .Q(ra), .clk(clock), .clr(Reset));
  Comparator #(.width(4), .mode("unsigned")) comparator_15 (.a(n23[10:7]), .b(4'b0011), .eq(n72));  // open: gt, lt
  Register #(.width(32)) x4 (.D(n60), .en(n77), .Q(x4_out), .clk(clock), .clr(Reset));
  Comparator #(.width(4), .mode("unsigned")) comparator_16 (.a(n23[10:7]), .b(4'b0110), .eq(n84));  // open: gt, lt
  Register #(.width(32)) u_x7 (.D(n60), .en(n89), .Q(x7), .clk(clock), .clr(Reset));
  Comparator #(.width(4), .mode("unsigned")) comparator_17 (.a(n23[10:7]), .b(4'b1001), .eq(n96));  // open: gt, lt
  Register #(.width(32)) x10 (.D(n60), .en(n101), .Q(a0), .clk(clock), .clr(Reset));
  Comparator #(.width(4), .mode("unsigned")) comparator_18 (.a(n23[10:7]), .b(4'b1100), .eq(n108));  // open: gt, lt
  Register #(.width(32)) u_x13 (.D(n60), .en(n113), .Q(x13), .clk(clock), .clr(Reset));
  Comparator #(.width(4), .mode("unsigned")) comparator_19 (.a(n23[10:7]), .b(4'b1111), .eq(n120));  // open: gt, lt
  not not_2 (illegal, n59);
  Comparator #(.width(7), .mode("unsigned")) comparator_20 (.a(n23[6:0]), .b(7'b0010011), .eq(n36));  // open: gt, lt
  not not_3 (n42, n41);
  Multiplexer #(.width(32), .select(1), .enable("false")) multiplexer_3 (.in0(n49), .in1(n52), .out(n61), .sel(n38));
  and and_15 (n73, n59, n72);
  and and_16 (n85, n59, n84);
  and and_17 (n97, n59, n96);
  and and_18 (n109, n59, n108);
  and and_19 (n121, n59, n120);

  assign x0_out = {32{1'b0}};

  // Other names for the same wires on the sheet: n24[6:0] = n23[6:0]; n25[4:0] = n23[11:7]; n29[3:0] = n23[10:7];
  //   n30 = n23[11]; n26[2:0] = n23[14:12]; n27[4:0] = n23[19:15]; n31[3:0] = n23[18:15]; n32 = n23[19];
  //   n28[11:0] = n23[31:20]; n53[1:0] = n52[1:0]; n54[29:0] = n52[31:2]; n123 = illegal; n125 = halt;
  //   n20[1:0] = PC_out[1:0]; PC[31:0] = PC_out; n21[5:0] = PC_out[7:2]; n22[23:0] = PC_out[31:8]; x1[31:0] = ra;
  //   x2[31:0] = x2_out; x3[31:0] = x3_out; x4[31:0] = x4_out; x5[31:0] = x5_out; x6[31:0] = x6_out; x10[31:0] = a0

  // Notes on the sheet:
  //   contents of rom_1 (hex, n*v repeats v):
  //   fff00113 110193 80000213 7ff00293 6300013 1d00313 30367 1c00067
endmodule
