// Logisim project mux4x3.circ as structural Verilog: 1 circuit, main circuit mux4x3
module mux4x3 (
  input  S0,
  input  S1,
  input  D0_0,
  input  D0_1,
  input  D0_2,
  input  D1_0,
  input  D1_1,
  input  D1_2,
  input  D2_0,
  input  D2_1,
  input  D2_2,
  input  D3_0,
  input  D3_1,
  input  D3_2,
  output Y0,
  output Y1,
  output Y2
);

  wire n0, n1, n2, n3, n4, n5, n6, n7, n8, n9, n10, n11, n13, n14, n15, n16, n17, n18, n20, n21, n22, n23,
       n24, n25;

  not not_1 (n0, S0);
  not not_2 (n1, S1);
  and and_1 (n2, n0, n1);
  and and_2 (n3, S0, n1);
  and and_3 (n4, n0, S1);
  and and_4 (n5, S0, S1);
  and and_5 (n6, n2, D0_0);
  and and_6 (n7, n3, D1_0);
  and and_7 (n8, n4, D2_0);
  and and_8 (n9, n5, D3_0);
  or or_1 (n10, n6, n7);
  or or_2 (n11, n10, n8);
  or or_3 (Y0, n11, n9);
  and and_9 (n13, n2, D0_1);
  and and_10 (n14, n3, D1_1);
  and and_11 (n15, n4, D2_1);
  and and_12 (n16, n5, D3_1);
  or or_4 (n17, n13, n14);
  or or_5 (n18, n17, n15);
  or or_6 (Y1, n18, n16);
  and and_13 (n20, n2, D0_2);
  and and_14 (n21, n3, D1_2);
  and and_15 (n22, n4, D2_2);
  and and_16 (n23, n5, D3_2);
  or or_7 (n24, n20, n21);
  or or_8 (n25, n24, n22);
  or or_9 (Y2, n25, n23);
endmodule
