// Logisim project scpu.circ as structural Verilog: 1 circuit, main circuit scpu
module scpu (
  input  Reset,
  output [7:0] R0_out,
  output [7:0] R1_out,
  output [7:0] R2_out,
  output [7:0] R3_out,
  output [3:0] PC_out,
  output halt
);

  wire clock, n22, n24, n26, n27, n32, n33, n34, n41, n42, n45, n46, n49, n50, n53, n54;
  wire [3:0] n36, n38;
  wire [7:0] n9, n19, n20, n28, n30, n31;

  Clock clock_1 (.out(clock));
  Comparator #(.width(2), .mode("unsigned")) comparator_1 (.a(n9[7:6]), .b(2'b00), .eq(n24));  // open: gt, lt
  assign n30 = {{4{1'b0}}, n9[3:0]};  // Bit_Extender bit_extender_1
  and and_1 (n42, n27, n41);
  Register #(.width(8)) R1 (.D(n31), .en(n46), .Q(R1_out), .clk(clock), .clr(Reset));
  Multiplexer #(.width(8), .select(2), .enable("false")) multiplexer_1 (
    .in0(R0_out), .in1(R1_out), .in2(R2_out), .in3(R3_out), .out(n19), .sel(n9[3:2]));
  Multiplexer #(.width(8), .select(1), .enable("false")) multiplexer_2 (.in0(n28), .in1(n30), .out(n31), .sel(n22));
  Adder #(.width(4)) adder_1 (.a(PC_out), .b(4'b0001), .out(n36), .cin(1'b0));  // open: cout
  Register #(.width(8)) R0 (.D(n31), .en(n42), .Q(R0_out), .clk(clock), .clr(Reset));
  Multiplexer #(.width(8), .select(2), .enable("false")) multiplexer_3 (
    .in0(R0_out), .in1(R1_out), .in2(R2_out), .in3(R3_out), .out(n20), .sel(n9[1:0]));
  Comparator #(.width(2), .mode("unsigned")) comparator_2 (.a(n9[7:6]), .b(2'b11), .eq(n26));  // open: gt, lt
  Comparator #(.width(8), .mode("unsigned")) comparator_3 (.a(R0_out), .b(n20), .eq(n32));  // open: gt, lt
  Multiplexer #(.width(4), .select(1), .enable("false")) multiplexer_4 (.in0(n36), .in1(n9[5:2]), .out(n38), .sel(n34));
  Comparator #(.width(2), .mode("unsigned")) comparator_4 (.a(n9[5:4]), .b(2'b11), .eq(n53));  // open: gt, lt
  Comparator #(.width(4), .mode("unsigned")) comparator_5 (.a(PC_out), .b(4'b0111), .eq(halt));  // open: gt, lt
  ROM #(.addrWidth(4), .dataWidth(8)) rom_1 (.addr(PC_out), .data(n9));
  or or_1 (n27, n22, n24);
  not not_1 (n33, n32);
  Register #(.width(4)) PC (.D(n38), .en(1'b1), .Q(PC_out), .clk(clock), .clr(Reset));
  Comparator #(.width(2), .mode("unsigned")) comparator_6 (.a(n9[5:4]), .b(2'b10), .eq(n49));  // open: gt, lt
  and and_2 (n54, n27, n53);
  Comparator #(.width(2), .mode("unsigned")) comparator_7 (.a(n9[7:6]), .b(2'b10), .eq(n22));  // open: gt, lt
  and and_3 (n34, n26, n33);
  Comparator #(.width(2), .mode("unsigned")) comparator_8 (.a(n9[5:4]), .b(2'b01), .eq(n45));  // open: gt, lt
  and and_4 (n50, n27, n49);
  Register #(.width(8)) R3 (.D(n31), .en(n54), .Q(R3_out), .clk(clock), .clr(Reset));
  Adder #(.width(8)) adder_2 (.a(n19), .b(n20), .out(n28), .cin(1'b0));  // open: cout
  Comparator #(.width(2), .mode("unsigned")) comparator_9 (.a(n9[5:4]), .b(2'b00), .eq(n41));  // open: gt, lt
  and and_5 (n46, n27, n45);
  Register #(.width(8)) R2 (.D(n31), .en(n50), .Q(R2_out), .clk(clock), .clr(Reset));

  // Other names for the same wires on the sheet: n10[1:0] = n9[1:0]; n14[3:0] = n9[3:0]; n16[1:0] = n9[1:0];
  //   n11[1:0] = n9[3:2]; n17[3:0] = n9[5:2]; n12[1:0] = n9[5:4]; n15[3:0] = n9[7:4]; n13[1:0] = n9[7:6];
  //   n18[1:0] = n9[7:6]; n57 = halt; PC[3:0] = PC_out; R0[7:0] = R0_out; R1[7:0] = R1_out; R2[7:0] = R2_out;
  //   R3[7:0] = R3_out

  // Notes on the sheet:
  //   contents of rom_1 (hex, n*v repeats v):
  //   8b 91 a0 b1 29 17 d1 df
endmodule
