// Logisim project sum10.circ as structural Verilog: 1 circuit, main circuit sum10
module sum10 (
  input  Reset,
  output [7:0] Index,
  output [7:0] Sum,
  output halt
);

  wire clock, n8;
  wire [7:0] n9, n12;

  Clock clock_1 (.out(clock));
  Adder #(.width(8)) adder_1 (.a(Index), .b(8'h1), .out(n9), .cin(1'b0));  // open: cout
  Register #(.width(8)) u_index (.D(n9), .en(n8), .Q(Index), .clk(clock), .clr(Reset));
  Comparator #(.width(8), .mode("unsigned")) comparator_1 (.a(Index), .b(8'ha), .eq(halt));  // open: gt, lt
  Adder #(.width(8)) adder_2 (.a(Sum), .b(n9), .out(n12), .cin(1'b0));  // open: cout
  not not_1 (n8, halt);
  Register #(.width(8)) u_sum (.D(n12), .en(n8), .Q(Sum), .clk(clock), .clr(Reset));

  // Other names for the same wires on the sheet: n7 = halt
endmodule
